# Fritzing sketch WateringSystem (saved by Fritzing 0.7.11b)
breadboards: 1

parts:
  Relay = Arduino Power Driver Shield
  Light_Sensor = Ambient Light Sensor (TEMT6000 Breakout Board)
  RTC = Real Time Clock Module - DS1307 RTC Breakout Board
  LED1 = LED - 3mm [color="Green (570nm)" package="3 mm [THT]"]
  S1 = Toggle Switch [package=THT]
  RHT1 = Humidity and Temperature Sensor RHT03
  Arduino1 = Arduino  # not connected
  LED2 = LED - 3mm [color="Red (633nm)" package="3 mm [THT]"]
  R1 = Resistor [tolerance=±1% resistance=470 package=THT]
  LED3 = LED - 3mm [color="Red (633nm)" package="3 mm [THT]"]
  LED4 = LED - 3mm [color="Red (633nm)" package="3 mm [THT]"]
  LED5 = LED - 3mm [color="Red (633nm)" package="3 mm [THT]"]
  LED6 = LED - 3mm [color="Red (633nm)" package="3 mm [THT]"]
  R2 = Resistor [tolerance=±1% resistance=470 package=THT]
  R3 = Resistor [tolerance=±1% resistance=470 package=THT]
  R4 = Resistor [tolerance=±1% resistance=470 package=THT]
  R5 = Resistor [tolerance=±1% resistance=470 package=THT]
  J1 = Screw terminal - 2 pins [package=THT]
  Power_plug1 = Power plug
  L1 = Solenoid
  L2 = Solenoid
  R6 = Resistor [tolerance=±1% resistance=470 package=THT]

nets:
  N1: Relay.D5-12V, L2.pin1
  N2: Relay.12V, L1.pin2, L2.pin2
  N3: Relay.D3-12V, L1.pin1
  5V: Relay.5V_ARDUINO, RTC.5V, LED1.cathode, S1.COM, RHT1.Vcc, R1.Pin_0, R2.Pin_0, R3.Pin_0, R4.Pin_0, R5.Pin_0
  N4: Relay.A0, Light_Sensor.S
  N5: Relay.A4, RTC.SDA
  N6: Relay.A5, RTC.SCL
  N7: Relay.D2, RHT1.Data-signal
  GND: Relay.GND, Light_Sensor.GND, RTC.GND, RHT1.GND_1, LED2.cathode, LED3.cathode, LED4.cathode, LED5.cathode, LED6.cathode
  N8: Light_Sensor.VCC, S1.L2, R6.Pin_0
  N9: LED1.anode, R6.Pin_1
  N10: LED2.anode, R1.Pin_1
  N11: LED3.anode, R2.Pin_1
  N12: LED4.anode, R3.Pin_1
  N13: LED5.anode, R4.Pin_1
  N14: LED6.anode, R5.Pin_1
  N15: J1.pin1, Power_plug1.VCC
  N16: J1.pin2, Power_plug1.GND

notes:
  X5 Seloinds
  Automatic Watering System
